# Fritzing sketch cyclic_volt (saved by Fritzing 0.9.9b)
breadboards: 1

parts:
  Part1 = Arduino Uno (Rev3)
  Power1 = PowerBRICK 12V
  Part2 = Adafruit MCP4725 Breakout Board - 12-Bit DAC [part_number="Adafruit #935"]
  IC2 = IC, DIP package, 8 pins [chip_label=IC]
  IC3 = IC, DIP package, 8 pins [chip_label=IC]
  IC4 = IC, DIP package, 8 pins [chip_label=IC]
  R1 = Resistor [tolerance=±5% resistance=220 package="1206 [SMD]"]
  IC1 = IC, DIP package, 8 pins [chip_label=IC]
  R2 = Resistor [tolerance=±5% resistance=33k package="1206 [SMD]"]
  R3 = Resistor [tolerance=±5% resistance=3.3k package="1206 [SMD]"]
  R4 = Resistor [tolerance=±5% resistance=220 package="1206 [SMD]"]
  R5 = Resistor [tolerance=±5% resistance=33k package="1206 [SMD]"]
  R6 = Resistor [tolerance=±5% resistance=33k package="1206 [SMD]"]
  C1 = Ceramic Capacitor [capacitance=100nF voltage=35V package="100 mil [THT, multilayer]"]
  C2 = Ceramic Capacitor [capacitance=100nF voltage=35V package="100 mil [THT, multilayer]"]
  C3 = Ceramic Capacitor [capacitance=100nF voltage=35V package="100 mil [THT, multilayer]"]
  R7 = Resistor [tolerance=±5% resistance=680 package="1206 [SMD]"]
  R8 = Resistor [tolerance=±5% power=0.25 resistance=330 package=THT]
  R9 = Resistor [tolerance=±5% power=0.25 resistance=330 package=THT]
  R10 = Resistor [tolerance=±5% power=0.25 resistance=330 package=THT]
  R11 = Resistor [tolerance=±5% power=0.25 resistance=220 package=THT]
  R12 = Resistor [tolerance=±5% power=0.25 resistance=220 package=THT]
  R13 = Resistor [tolerance=±5% power=0.25 resistance=220 package=THT]

nets:
  N1: Part1.A0, Part2.A0
  N2: Part1.A1, IC4.pin1, R12.Pin_0
  N3: Part1.A4/SDA, Part2.SDA
  N4: Part1.A5/SCL, Part2.SCL
  GND: Part1.GND, Power1.GND, Part2.GND, IC3.pin5, IC4.pin5, R2.Pin_1, C2.0, R13.Pin_1
  N5: Part1.D3_PWM, R6.Pin_1
  N6: Part1.3V3, R11.Pin_0
  5V: Part1.5V, Part2.VDD
  N7: Power1.-Vout, IC2.pin4, IC3.pin4, IC1.pin4
  N8: Power1.+Vout, IC2.pin8, IC3.pin8, IC4.pin4, IC4.pin8, IC1.pin8
  N9: Part2.VOUT, IC1.pin3
  N10: IC2.pin1, IC2.pin2, R4.Pin_1, C1.0
  N11: IC2.pin3, R5.Pin_0, C2.1
  N12: IC2.pin5, IC1.pin7, R3.Pin_1
  N13: IC3.pin1, IC3.pin2, R8.Pin_0
  N14: IC3.pin3, IC3.pin7, C3.1, R7.Pin_1
  N15: IC3.pin6, C3.0, R7.Pin_0
  N16: IC4.pin2, R12.Pin_1, R13.Pin_0
  N17: IC4.pin3, R10.Pin_1, R11.Pin_1
  N18: IC4.pin6, R8.Pin_1, R9.Pin_0
  N19: IC4.pin7, R9.Pin_1, R10.Pin_0
  N20: R1.Pin_0, IC1.pin1, IC1.pin2
  N21: R1.Pin_1, IC1.pin5, R2.Pin_0
  N22: IC1.pin6, R3.Pin_0, R4.Pin_0
  N23: R5.Pin_1, R6.Pin_0, C1.1

custom parts:
  PowerBRICK 12V: PowerBRICKs are split-rail power supply modules that are intended to be used with a breadboard. These generate both a negative and positive voltage out of a single 5V USB voltage.
  Adafruit MCP4725 Breakout Board - 12-Bit DAC: Your microcontroller probably has an ADC (analog -> digital converter) but does it have a DAC (digital -> analog converter)??? Now it can! This breakout board features the easy-to-use MCP4725 12-bit DAC. Control it via I2C and send it the value you want it to output, and the VOUT pin will have it. Great for audio / analog projects, such as when you can't use PWM but need a sine wave or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
